// Digital circuit cpu.dig as structural Verilog
module cpu (
  input  clk,
  input  clk_2
);

  wire nand_1_out, nand_2_out, oprom_1_bssel, oprom_1_fwen, oprom_1_massel, oprom_1_mwen, oprom_1_rwen;
  wire [1:0] oprom_1_pcssel, oprom_1_rssel;
  wire [2:0] program_memory_1_aluop, program_memory_1_rd, program_memory_1_ro1, program_memory_1_ro2;
  wire [3:0] program_memory_1_opcode;
  wire [7:0] _2x8bit_mux_1_out, _4x8bit_mux_1_out, _8bit_alu_1_result, program_memory_1_imm8,
       ramdualport_1_d, register_file_1_p9;
  wire [15:0] _2x16bit_mux_1_p4, _4x16bit_mux_1_out, _16bit_incrementer_1_out, program_counter_1_r,
       program_memory_1_imm16, register_file_1_p7;

  nand nand_1 (nand_1_out, clk_2, clk_2);
  program_memory program_memory_1 (
    .ADR(program_counter_1_r), .OPCODE(program_memory_1_opcode), .RD(program_memory_1_rd),
    .RO1(program_memory_1_ro1), .RO2(program_memory_1_ro2), .IMM8(program_memory_1_imm8),
    .IMM16(program_memory_1_imm16), .ALUOP(program_memory_1_aluop));  // open: COND
  program_counter program_counter_1 (.CLK(clk_2), .W(_4x16bit_mux_1_out), .R(program_counter_1_r));
  _4x16bit_mux _4x16bit_mux_1 (
    .SEL(oprom_1_pcssel), .IN0({16{1'b0}}), .IN1(_16bit_incrementer_1_out), .IN2(register_file_1_p7),
    .IN3(program_memory_1_imm16), .OUT(_4x16bit_mux_1_out));
  oprom oprom_1 (
    .OPCODE(program_memory_1_opcode), .SKIP(1'b0), .RWEN(oprom_1_rwen), .FWEN(oprom_1_fwen),
    .MWEN(oprom_1_mwen), .BSSEL(oprom_1_bssel), .MASSEL(oprom_1_massel), .RSSEL(oprom_1_rssel),
    .PCSSEL(oprom_1_pcssel));
  _16bit_incrementer _16bit_incrementer_1 (.IN(program_counter_1_r), .OUT(_16bit_incrementer_1_out));
  _4x8bit_mux _4x8bit_mux_1 (
    .SEL(oprom_1_rssel), .IN0(program_memory_1_imm8), .IN1(ramdualport_1_d), .IN2(_8bit_alu_1_result),
    .IN3(register_file_1_p7[7:0]), .OUT(_4x8bit_mux_1_out));
  // register_file register_file_1: pin names not known; wires that end beside it: nand_1_out, oprom_1_rwen, _4x8bit_mux_1_out, program_memory_1_ro2, program_memory_1_ro1, program_memory_1_rd, register_file_1_p7[7:0], register_file_1_p7[15:8], register_file_1_p9
  // _2x16bit_mux _2x16bit_mux_1: pin names not known; wires that end beside it: oprom_1_massel, program_memory_1_imm16, {register_file_1_p9, register_file_1_p7[7:0]}, _2x16bit_mux_1_p4
  _2x8bit_mux _2x8bit_mux_1 (
    .SEL(oprom_1_bssel), .B(register_file_1_p7[15:8]), .A(program_memory_1_imm8), .OUT(_2x8bit_mux_1_out));
  nand nand_2 (nand_2_out, oprom_1_mwen, oprom_1_mwen);
  _8bit_alu _8bit_alu_1 (
    .A(register_file_1_p7[7:0]), .B(_2x8bit_mux_1_out), .OP(program_memory_1_aluop), .CLK(nand_1_out),
    .WFLAGEN(oprom_1_fwen), .RESULT(_8bit_alu_1_result));  // open: FLAGS
  RAMDualPort #(.AddrBits(16), .Bits(8)) ramdualport_1 (
    .A(_2x16bit_mux_1_p4), .Din(register_file_1_p7[15:8]), .str(oprom_1_mwen), .C(clk), .ld(nand_2_out),
    .D(ramdualport_1_d));

  // Notes on the sheet:
  //   clk: Hz: 100
endmodule
